// Logisim project Two-Digit-7seg-Display.circ as structural Verilog: 1 circuit, main circuit main
module main (
  input  in_1,
  input  in_2,
  input  in_3,
  input  in_4,
  input  in_5,
  input  in_6,
  input  in_7,
  input  in_8,
  input  in_9
);

  wire A_out, and_1_out, and_2_out, and_3_out, and_4_out, and_5_out, and_6_out, and_7_out, and_8_out,
       and_9_out, and_10_out, and_11_out, and_12_out, and_13_out, and_14_out, and_15_out, and_16_out,
       and_17_out, and_18_out, and_19_out, and_20_out, and_21_out, and_22_out, and_23_out, and_24_out,
       and_25_out, and_26_out, and_27_out, and_28_out, and_29_out, and_30_out, and_31_out, and_32_out, B_out,
       C_out, D_out, E_out, F_out, G_out, multiplexer_1_out, multiplexer_2_out, multiplexer_3_out,
       multiplexer_4_out, not_1_out, not_2_out, not_3_out, not_4_out, not_5_out, not_6_out, not_7_out,
       not_8_out, not_9_out, not_10_out, not_11_out;

  Multiplexer multiplexer_1 (.in0(in_1), .in1(in_2), .out(multiplexer_1_out), .sel(in_4));  // open: en
  Multiplexer multiplexer_2 (.in0(in_3), .in1(in_5), .out(multiplexer_2_out), .sel(in_4));  // open: en
  Multiplexer multiplexer_3 (.in0(in_6), .in1(in_7), .out(multiplexer_3_out), .sel(in_4));  // open: en
  Multiplexer multiplexer_4 (.in0(in_8), .in1(in_9), .out(multiplexer_4_out), .sel(in_4));  // open: en
  not not_1 (not_1_out, multiplexer_1_out);
  not not_2 (not_2_out, multiplexer_2_out);
  not not_3 (not_3_out, multiplexer_3_out);
  not not_4 (not_4_out, multiplexer_4_out);
  and and_1 (and_1_out, not_2_out, multiplexer_3_out);
  and and_2 (and_2_out, not_1_out, multiplexer_2_out);
  and and_3 (and_3_out, multiplexer_2_out, not_3_out, not_4_out);
  and and_4 (and_4_out, not_2_out, multiplexer_3_out);
  and and_5 (and_5_out, not_1_out, multiplexer_3_out);
  and and_6 (and_6_out, not_1_out, not_2_out);
  and and_7 (and_7_out, multiplexer_2_out, not_1_out);
  and and_8 (and_8_out, not_1_out, not_3_out);
  and and_9 (and_9_out, not_1_out, multiplexer_2_out);
  and and_10 (and_10_out, multiplexer_2_out, not_3_out, not_4_out);
  and and_11 (and_11_out, multiplexer_1_out, not_2_out, multiplexer_3_out);
  and and_12 (and_12_out, not_1_out, not_2_out, not_3_out);
  and and_13 (and_13_out, multiplexer_3_out, not_4_out);
  and and_14 (and_14_out, multiplexer_1_out, multiplexer_2_out);
  and and_15 (and_15_out, not_1_out, not_2_out);
  and and_16 (and_16_out, not_3_out, not_4_out);
  and and_17 (and_17_out, multiplexer_1_out, multiplexer_3_out);
  and and_18 (and_18_out, not_1_out, not_2_out, not_3_out);
  or G (G_out, multiplexer_4_out, and_1_out, and_2_out, and_3_out);
  or F (F_out, multiplexer_4_out, and_4_out, and_5_out, and_6_out);
  or E (E_out, and_7_out, and_8_out);
  or D (D_out, and_9_out, and_10_out, multiplexer_4_out, and_11_out, and_12_out);
  or C (C_out, multiplexer_1_out, not_2_out, and_13_out);
  or B (B_out, multiplexer_4_out, and_14_out, and_15_out, and_16_out);
  or A (A_out, multiplexer_2_out, multiplexer_4_out, and_17_out, and_18_out);
  not not_5 (not_5_out, in_4);
  not not_6 (not_6_out, in_4);
  not not_7 (not_7_out, in_4);
  _7_Segment_Display u_7_segment_display_1 (
    .g(and_20_out), .f(and_22_out), .a(and_32_out), .b(and_30_out), .e(and_24_out), .d(and_26_out),
    .c(and_28_out));  // open: dp
  and and_19 (and_19_out, in_4, G_out);
  and and_20 (and_20_out, not_5_out, G_out);
  and and_21 (and_21_out, in_4, F_out);
  and and_22 (and_22_out, not_6_out, F_out);
  and and_23 (and_23_out, in_4, E_out);
  and and_24 (and_24_out, not_7_out, E_out);
  and and_25 (and_25_out, in_4, D_out);
  not not_8 (not_8_out, in_4);
  and and_26 (and_26_out, not_8_out, D_out);
  and and_27 (and_27_out, in_4, C_out);
  not not_9 (not_9_out, in_4);
  and and_28 (and_28_out, not_9_out, C_out);
  and and_29 (and_29_out, in_4, B_out);
  not not_10 (not_10_out, in_4);
  and and_30 (and_30_out, not_10_out, B_out);
  and and_31 (and_31_out, in_4, A_out);
  not not_11 (not_11_out, in_4);
  and and_32 (and_32_out, not_11_out, A_out);
  _7_Segment_Display u_7_segment_display_2 (
    .g(and_19_out), .f(and_21_out), .a(and_31_out), .b(and_29_out), .e(and_23_out), .d(and_25_out),
    .c(and_27_out));  // open: dp

  // Notes on the sheet:
  //   Digit Cycle Circuit
  //   x3
  //   x2
  //   x1
  //   x0
  //   BCD-to-7 Segment Decoding Circuit
endmodule
